// Logisim project Regfile.circ as structural Verilog: 1 circuit, main circuit main
module main (
  input  [1:0] Read_register_1,
  input  [1:0] Read_register_2,
  input  [1:0] write_register,
  input  [15:0] write_data,
  input  RegWrite,
  input  clock,
  output [15:0] Reg_0_Value,
  output [15:0] Reg_1_Value,
  output [15:0] Reg_2_Value,
  output [15:0] Reg_3_Value,
  output [15:0] Read_Data_1,
  output [15:0] Read_Data_2
);

  wire [15:0] multiplexer_1_out, multiplexer_3_out, multiplexer_5_out, multiplexer_6_out, WriteReg0,
       WriteReg1, WriteReg2, WriteReg3;

  Multiplexer #(.select(2), .width(16)) multiplexer_1 (
    .in0(WriteReg0), .in1(Reg_0_Value), .in2(Reg_0_Value), .in3(Reg_0_Value), .out(multiplexer_1_out),
    .sel(write_register));  // open: en
  Register #(.width(16)) register_1 (.D(multiplexer_1_out), .Q(Reg_0_Value), .clk(clock));  // open: en, clr
  Multiplexer #(.select(2), .width(16)) multiplexer_2 (
    .in0(Reg_0_Value), .in1(Reg_1_Value), .in2(Reg_2_Value), .in3(Reg_3_Value), .out(Read_Data_1),
    .sel(Read_register_1));  // open: en
  Register #(.width(16)) register_2 (.D(multiplexer_3_out), .Q(Reg_1_Value), .clk(clock));  // open: en, clr
  Multiplexer #(.select(2), .width(16)) multiplexer_3 (
    .in0(Reg_1_Value), .in1(WriteReg1), .in2(Reg_1_Value), .in3(Reg_1_Value), .out(multiplexer_3_out),
    .sel(write_register));  // open: en
  Multiplexer #(.select(2), .width(16)) multiplexer_4 (
    .in0(Reg_0_Value), .in1(Reg_1_Value), .in2(Reg_2_Value), .in3(Reg_3_Value), .out(Read_Data_2),
    .sel(Read_register_2));  // open: en
  Register #(.width(16)) register_3 (.D(multiplexer_5_out), .Q(Reg_2_Value), .clk(clock));  // open: en, clr
  Multiplexer #(.select(2), .width(16)) multiplexer_5 (
    .in0(Reg_2_Value), .in1(Reg_2_Value), .in2(WriteReg2), .in3(Reg_2_Value), .out(multiplexer_5_out),
    .sel(write_register));  // open: en
  Demultiplexer #(.select(2), .width(16)) demultiplexer_1 (
    .out0(WriteReg0), .out1(WriteReg1), .out2(WriteReg2), .out3(WriteReg3), .in(write_data),
    .sel(write_register), .en(RegWrite));
  Register #(.width(16)) register_4 (.D(multiplexer_6_out), .Q(Reg_3_Value), .clk(clock));  // open: en, clr
  Multiplexer #(.select(2), .width(16)) multiplexer_6 (
    .in0(Reg_3_Value), .in1(Reg_3_Value), .in2(Reg_3_Value), .in3(WriteReg3), .out(multiplexer_6_out),
    .sel(write_register));  // open: en

  // Other names for the same wires on the sheet: CLK = clock; ReadData1[15:0] = Read_Data_1;
  //   ReadData2[15:0] = Read_Data_2; ReadReg2[1:0] = Read_register_2; Reg0[15:0] = Reg_0_Value;
  //   Reg1[15:0] = Reg_1_Value; Reg2[15:0] = Reg_2_Value; Reg3[15:0] = Reg_3_Value; writeData[15:0] = write_data;
  //   writeReg[1:0] = write_register

  // Notes on the sheet:
  //   These are INPUTS to the circuit
  //   These are INPUTS to the circuit
  //   DO NOT CHANGE THE LOCATIONS OF THE INPUTS/OUTPUTS! IF YOU DO SO, YOU NEED TO MAKE SURE THE PINS ARE AT THE RIGHT PLACE!
  //   These are OUTPUTS to the circuit
  //   Yet again, the clock is not an actual clock, but an input, one that will be driven from a higher circuit
  //   These are OUTPUTS to the circuit
endmodule
