// Logisim project alu.circ as structural Verilog: 5 circuits, main circuit main
module main (
  input  [15:0] X,
  input  [15:0] Y,
  input  [3:0] Switch__S,
  output Signed_Overflow,
  output [15:0] RESULT,
  output Equal
);

  wire comparator_1_lt, or_2_out, or_3_out, overflow1, overflow2, overflow8a, overflow8b, overflow9a,
       overflow9b;
  wire [3:0] bit_extender_1_out, bit_extender_2_out, bit_extender_3_out;
  wire [7:0] n8bitadd_1_out_2, n8bitadd_2_out_2, n8bitsuboverflow_1_out_2, n8bitsuboverflow_2_out_2;
  wire [15:0] and_1_out, bit_extender_4_out, n16bitadd_1_out_2, n16bitsuboverflow_1_out_2, or_1_out,
       shifter_1_out, shifter_2_out, shifter_3_out, shifter_4_out;

  _8BitAdd u_8bitadd_1 (.in_1(Y[7:0]), .in_2(X[7:0]), .out(overflow8a), .out_2(n8bitadd_1_out_2));
  _8BitAdd u_8bitadd_2 (.in_1(Y[15:8]), .in_2(X[15:8]), .out(overflow8b), .out_2(n8bitadd_2_out_2));
  _8BitSubOverflow u_8bitsuboverflow_1 (
    .in_1(Y[7:0]), .in_2(X[7:0]), .out(overflow9a), .out_2(n8bitsuboverflow_1_out_2));
  _8BitSubOverflow u_8bitsuboverflow_2 (
    .in_1(Y[15:8]), .in_2(X[15:8]), .out(overflow9b), .out_2(n8bitsuboverflow_2_out_2));
  _16BitSubOverflow u_16bitsuboverflow_1 (.in_1(X), .in_2(Y), .out(overflow2), .out_2(n16bitsuboverflow_1_out_2));
  Bit_Extender #(.in_width(16), .out_width(4)) bit_extender_1 (.in(Y), .out(bit_extender_1_out));
  Bit_Extender #(.in_width(16), .out_width(4)) bit_extender_2 (.in(Y), .out(bit_extender_2_out));
  Bit_Extender #(.in_width(16), .out_width(4), .\type ("sign")) bit_extender_3 (.in(Y), .out(bit_extender_3_out));
  Comparator #(.width(16)) comparator_1 (.a(X), .b(Y), .lt(comparator_1_lt));  // open: gt, eq
  _16BitAdd u_16bitadd_1 (.in_1(X), .in_2(Y), .out(overflow1), .out_2(n16bitadd_1_out_2));
  Shifter #(.width(16)) shifter_1 (.in(X), .\dist (bit_extender_1_out), .out(shifter_1_out));
  Shifter #(.width(16), .shift("lr")) shifter_2 (.in(X), .\dist (bit_extender_2_out), .out(shifter_2_out));
  Shifter #(.width(16), .shift("ar")) shifter_3 (.in(X), .\dist (bit_extender_3_out), .out(shifter_3_out));
  assign bit_extender_4_out = {{15{1'b0}}, comparator_1_lt};  // Bit_Extender bit_extender_4
  assign or_1_out = X | Y;  // OR_Gate or_1, 16 bits wide
  assign and_1_out = X & Y;  // AND_Gate and_1, 16 bits wide
  Multiplexer #(.select(4), .width(16)) multiplexer_1 (
    .in0(n16bitadd_1_out_2), .in1(n16bitsuboverflow_1_out_2), .in2(shifter_1_out), .in3(shifter_2_out),
    .in4(shifter_3_out), .in5(bit_extender_4_out), .in6(or_1_out), .in7(and_1_out),
    .in8({n8bitadd_2_out_2, n8bitadd_1_out_2}), .in9({n8bitsuboverflow_2_out_2, n8bitsuboverflow_1_out_2}),
    .in10(shifter_4_out), .out(RESULT), .sel(Switch__S));  // open: in11, in12, in13, in14, in15, en
  Shifter #(.width(16)) shifter_4 (.in(Y), .\dist (4'b1000), .out(shifter_4_out));
  or or_2 (or_2_out, overflow8a, overflow8b);
  or or_3 (or_3_out, overflow9a, overflow9b);
  Multiplexer #(.select(4)) multiplexer_2 (
    .in0(overflow1), .in1(overflow2), .in2(1'b0), .in3(1'b0), .in4(1'b0), .in5(1'b0), .in6(1'b0), .in7(1'b0),
    .in8(or_2_out), .in9(or_3_out), .in10(1'b0), .in11(1'b0), .in12(1'b0), .in13(1'b0), .in14(1'b0),
    .in15(1'b0), .out(Signed_Overflow), .sel(Switch__S));  // open: en
  Comparator #(.width(16)) comparator_2 (.a(X), .b(Y), .eq(Equal));  // open: gt, lt

  // Other names for the same wires on the sheet: selector[3:0] = Switch__S; XLowerBits[7:0] = X[7:0];
  //   XHigherBits[7:0] = X[15:8]; YLowerBits[7:0] = Y[7:0]; YHigherBits[7:0] = Y[15:8]

  // Notes on the sheet:
  //   INPUTS to your circuit
  //   INPUT to your circuit
  //   DON'T CHANGE THE INPUTS AND OUTPUTS! IF YOU DO SO, YOU NEED TO MAKE SURE THE PINS ARE IN THE RIGHT PLACES!
  //   OUTPUTS of your circuit
endmodule

module _16BitSubOverflow (
  input  [15:0] in_1,
  input  [15:0] in_2,
  output out,
  output [15:0] out_2
);

  wire and_1_out;

  Subtractor #(.width(16)) subtractor_1 (.a(in_1), .b(in_2), .out(out_2));  // open: bin, bout
  and and_1 (and_1_out, in_2[15], out_2[15]);
  Multiplexer multiplexer_1 (.in0(1'b0), .in1(1'b1), .out(out), .sel(and_1_out));  // open: en

  // Other names for the same wires on the sheet: x[15:0] = in_1; y[15:0] = in_2
endmodule

module _8BitSubOverflow (
  input  [7:0] in_1,
  input  [7:0] in_2,
  output out,
  output [7:0] out_2
);

  wire and_1_out;

  Subtractor subtractor_1 (.a(in_1), .b(in_2), .out(out_2));  // open: bin, bout
  // Probe on in_1
  // Probe on in_2
  and and_1 (and_1_out, in_2[7], out_2[7]);
  Multiplexer multiplexer_1 (.in0(1'b0), .in1(1'b1), .out(out), .sel(and_1_out));  // open: en

  // Other names for the same wires on the sheet: x[7:0] = in_1; y[7:0] = in_2
endmodule

module _16BitAdd (
  input  [15:0] in_1,
  input  [15:0] in_2,
  output out,
  output [15:0] out_2
);

  wire and_1_out, and_2_out, not_1_out, xor_1_out, xor_2_out;

  Adder #(.width(16)) adder_1 (.a(in_1), .b(in_2), .out(out_2));  // open: cin, cout
  and and_1 (and_1_out, in_1[15], in_2[15]);
  xor xor_1 (xor_1_out, in_1[15], in_2[15]);
  not not_1 (not_1_out, xor_1_out);
  xor xor_2 (xor_2_out, and_1_out, out_2[15]);
  and and_2 (and_2_out, not_1_out, xor_2_out);
  Multiplexer multiplexer_1 (.in0(1'b0), .in1(1'b1), .out(out), .sel(and_2_out));  // open: en

  // Other names for the same wires on the sheet: x[15:0] = in_1; y[15:0] = in_2
endmodule

module _8BitAdd (
  input  [7:0] in_1,
  input  [7:0] in_2,
  output out,
  output [7:0] out_2
);

  wire and_1_out, and_2_out, not_1_out, xor_1_out, xor_2_out;

  Adder adder_1 (.a(in_1), .b(in_2), .out(out_2));  // open: cin, cout
  and and_1 (and_1_out, in_1[7], in_2[7]);
  xor xor_1 (xor_1_out, in_1[7], in_2[7]);
  not not_1 (not_1_out, xor_1_out);
  xor xor_2 (xor_2_out, and_1_out, out_2[7]);
  and and_2 (and_2_out, not_1_out, xor_2_out);
  Multiplexer multiplexer_1 (.in0(1'b0), .in1(1'b1), .out(out), .sel(and_2_out));  // open: en

  // Other names for the same wires on the sheet: x[7:0] = in_1; y[7:0] = in_2
endmodule
