// Logisim project cpu.circ as structural Verilog: 22 circuits, main circuit main
module main (
  input  [15:0] From_Instr_Mem,
  input  clk,
  output [15:0] r0,
  output [15:0] r1,
  output [15:0] r2,
  output [15:0] r3,
  output [15:0] Display_0,
  output [15:0] Display_1,
  output [15:0] To_Instr_Mem,
  output [15:0] Data_Mem_Data,
  output [15:0] Data_Mem_Addr,
  output Data_Mem_Write
);

  wire ALUequal, ALUop_t, ALUsrc, and_3_out, and_4_out, Beq, BEQGOOD, Bne, BNEGOOD, BoJ, button_1_out,
       Display, J, Jal, main_2_signed_overflow, MemToReg, not_1_out, not_2_out, not_3_out, or_1_out,
       RegWrite, Rtype, SignExt;
  wire [1:0] multiplexer_2_out, rd, RegDst, rt, splitter_1_rs;
  wire [2:0] nextPC_Selector;
  wire [3:0] alucontroller_1_opcode_2, ALUOp, splitter_1_opcode;
  wire [5:0] splitter_1_function;
  wire [7:0] splitter_1_imm;
  wire [11:0] jAddress, targetAddress;
  wire [15:0] adder_1_out, bit_extender_1_out, bit_extender_2_out, BranchOff, controlled_buffer_1_out,
       multiplexer_1_out, multiplexer_4_out, multiplexer_5_out, multiplexer_6_out, multiplexer_7_out, NextPC,
       NOop_instructionout, PC___1, RegWriteData, rs;
  wire [31:16] register_1_q;

  Register #(.width(16)) pc (.D(multiplexer_1_out), .Q(To_Instr_Mem), .clk(clk));  // open: en, clr
  Multiplexer #(.width(16)) multiplexer_1 (
    .in0(adder_1_out), .in1(NextPC), .out(multiplexer_1_out), .sel(BoJ));  // open: en
  Noop NOop (
    .Instruction(From_Instr_Mem), .nPC_sel(nextPC_Selector), .BEQGOOD(BEQGOOD), .ALUequal(ALUequal),
    .BNEGOOD(BNEGOOD), .Jump(or_1_out), .InstructionOut(NOop_instructionout));
  Adder #(.width(16)) adder_1 (.a(To_Instr_Mem), .b(16'h1), .out(adder_1_out));  // open: cin, cout
  Register #(.width(32)) register_1 (
    .D({NOop_instructionout, adder_1_out}), .Q({register_1_q, PC___1}), .clk(clk));  // open: en, clr
  or or_1 (or_1_out, Jal, J);
  splitter splitter_1 (
    .instruction_In(register_1_q), .\function (splitter_1_function), .rd(rd), .rt(rt), .rs(splitter_1_rs),
    .opCode(splitter_1_opcode), .target_Address(targetAddress), .imm(splitter_1_imm));
  // Probe on register_1_q
  PCcounter pccounter_1 (
    .PC(PC___1), .signExtImm(BranchOff), .BEQpass(BEQGOOD), .BNEpass(BNEGOOD), .jAddr(jAddress), .rs(rs),
    .npc_Sel(nextPC_Selector), .nxtPC(NextPC));
  Controller controller_1 (
    .opCode(splitter_1_opcode), .RegWrite(RegWrite), .MemWrite(Data_Mem_Write), .display(Display),
    .ALUOp(ALUOp), .Jal(Jal), .Jump(J), .Beq(Beq), .Bne(Bne), .MemToReg(MemToReg), .BranchOJump(BoJ),
    .SignExt(SignExt), .ALUsrc(ALUsrc), .RegDst(RegDst), .nPC_Sel(nextPC_Selector), .ALUoperation(ALUop_t),
    .Rtype(Rtype));
  // Probe on RegDst
  // Probe on rt
  // Probe on multiplexer_2_out
  assign bit_extender_1_out = {{8{1'b0}}, splitter_1_imm};  // Bit_Extender bit_extender_1
  assign bit_extender_2_out = {{8{splitter_1_imm[7]}}, splitter_1_imm};  // Bit_Extender bit_extender_2
  Multiplexer #(.select(2), .width(2), .enable("false")) multiplexer_2 (
    .in0(rt), .in1(rd), .in2(2'b11), .out(multiplexer_2_out), .sel(RegDst));  // open: in3
  Multiplexer #(.width(16), .enable("false")) multiplexer_3 (
    .in0(bit_extender_1_out), .in1(bit_extender_2_out), .out(BranchOff), .sel(SignExt));
  Bit_Extender #(.in_width(16), .out_width(12)) bit_extender_3 (.in(bit_extender_2_out), .out(jAddress));
  ALUcontroller alucontroller_1 (.opcode(ALUOp), .\function (splitter_1_function), .opcode_2(alucontroller_1_opcode_2));
  Regfile_main main_1 (
    .Read_register_1(splitter_1_rs), .Read_register_2(rt), .write_register(multiplexer_2_out),
    .write_data(RegWriteData), .Reg_0_Value(r0), .Reg_1_Value(r1), .Reg_2_Value(r2), .Reg_3_Value(r3),
    .RegWrite(RegWrite), .clock(clk), .Read_Data_1(rs), .Read_Data_2(Data_Mem_Data));
  Hex_Digit_Display hex_digit_display_1 (.value(Display_0[11:8]));  // open: dp
  Hex_Digit_Display hex_digit_display_2 (.value(Display_0[15:12]));  // open: dp
  Hex_Digit_Display hex_digit_display_3 (.value(Display_0[3:0]));  // open: dp
  Hex_Digit_Display hex_digit_display_4 (.value(Display_0[7:4]));  // open: dp
  and and_1 (BEQGOOD, Beq, ALUequal);
  Multiplexer #(.width(16), .enable("false")) multiplexer_4 (
    .in0(Data_Mem_Data), .in1(BranchOff), .out(multiplexer_4_out), .sel(ALUsrc));
  Hex_Digit_Display hex_digit_display_5 (.value(Display_1[11:8]));  // open: dp
  Hex_Digit_Display hex_digit_display_6 (.value(Display_1[15:12]));  // open: dp
  not not_1 (not_1_out, ALUequal);
  LED led_1 (.in(main_2_signed_overflow));
  alu_main main_2 (
    .Switch__S(alucontroller_1_opcode_2), .X(rs), .Equal(ALUequal), .RESULT(Data_Mem_Addr),
    .Signed_Overflow(main_2_signed_overflow), .Y(multiplexer_4_out));
  Hex_Digit_Display hex_digit_display_7 (.value(Display_1[7:4]));  // open: dp
  Hex_Digit_Display hex_digit_display_8 (.value(Display_1[3:0]));  // open: dp
  and and_2 (BNEGOOD, not_1_out, Bne);
  not not_2 (not_2_out, BranchOff[0]);
  Multiplexer #(.width(16)) multiplexer_5 (
    .in0(Display_1), .in1(rs), .out(multiplexer_5_out), .sel(and_3_out));  // open: en
  and and_3 (and_3_out, Display, BranchOff[0]);
  Multiplexer #(.width(16)) multiplexer_6 (
    .in0(Display_0), .in1(rs), .out(multiplexer_6_out), .sel(and_4_out));  // open: en
  and and_4 (and_4_out, Display, not_2_out);
  assign controlled_buffer_1_out = Data_Mem_Write ? Data_Mem_Data : 16'bz;  // Controlled_Buffer controlled_buffer_1
  RAM #(.addrWidth(16), .dataWidth(16)) ram_1 (
    .addr(Data_Mem_Addr), .data(controlled_buffer_1_out), .sel(1'b1), .clk(clk), .ld(not_3_out),
    .clr(button_1_out));
  not not_3 (not_3_out, Data_Mem_Write);
  Button button_1 (.out(button_1_out));
  Register #(.width(16)) register_2 (.D(multiplexer_5_out), .Q(Display_1), .clk(clk));  // open: en, clr
  Register #(.width(16)) register_3 (.D(multiplexer_6_out), .Q(Display_0), .clk(clk));  // open: en, clr
  Comparator #(.width(4)) comparator_1 (.a(ALUOp), .b(4'b1001), .eq(Data_Mem_Write));  // open: gt, lt
  Multiplexer #(.width(16)) multiplexer_7 (
    .in0(Data_Mem_Addr), .in1(controlled_buffer_1_out), .out(multiplexer_7_out), .sel(MemToReg));  // open: en
  Multiplexer #(.width(16)) multiplexer_8 (
    .in0(multiplexer_7_out), .in1(PC___1), .out(RegWriteData), .sel(Jal));  // open: en

  // Other names for the same wires on the sheet: ALU[15:0] = Data_Mem_Addr; d0[15:0] = Display_0;
  //   d1[15:0] = Display_1; in[15:0] = Data_Mem_Data; MemWrite = Data_Mem_Write

  // Notes on the sheet:
  //   This is the current PC that you need to send as OUTPUT
  //   This is the instruction that you would receive as INPUT
  //   This is a CLK that is an INPUT driven from the harness.
  //   Remember, this circuit is loaded from the harness to be tested!
  //   DO NOT CHANGE THE LOCATIONS OF THE INPUTS OR OUTPUTS! IF YOU DO SO, YOU NEED TO MAKE SURE THE PINS ARE IN THE RIGHT PLACES!
  //   These are OUTPUTS of the circuit
  //   These are OUTPUTS of the circuit
endmodule

// SPLITTER
module splitter (
  input  [15:0] instruction_In,
  output [5:0] \function ,
  output [1:0] rd,
  output [1:0] rt,
  output [1:0] rs,
  output [3:0] opCode,
  output [11:0] target_Address,
  output [7:0] imm
);


  assign \function  = instruction_In[5:0];
  assign imm = instruction_In[7:0];
  assign opCode = instruction_In[15:12];
  assign rd = instruction_In[7:6];
  assign rs = instruction_In[11:10];
  assign rt = instruction_In[9:8];
  assign target_Address = instruction_In[11:0];
endmodule

// CONTROL
module Controller (
  input  [3:0] opCode,
  output RegWrite,
  output MemWrite,
  output display,
  output [3:0] ALUOp,
  output Jal,
  output Jump,
  output Beq,
  output Bne,
  output MemToReg,
  output BranchOJump,
  output SignExt,
  output ALUsrc,
  output [1:0] RegDst,
  output [2:0] nPC_Sel,
  output ALUoperation,
  output Rtype
);

  RegWrite regwrite_1 (.opCode(opCode), .out_2(RegWrite));
  MemWrite memwrite_1 (.opCode(opCode), .out_2(MemWrite));
  Display display_1 (.opCode(opCode), .out_2(display));
  Jal jal_1 (.opCode(opCode), .out_2(Jal));
  Jump jump_1 (.opCode(opCode), .out_2(Jump));
  Beq beq_1 (.opCode(opCode), .out_2(Beq));
  Bne bne_1 (.opCode(opCode), .out_2(Bne));
  MemToReg memtoreg_1 (.opCode(opCode), .out_2(MemToReg));
  BranchOJump branchojump_1 (.opCode(opCode), .out_2(BranchOJump));
  SignExtend signextend_1 (.opCode(opCode), .SignExtend(SignExt));
  ALUsrc alusrc_1 (.opCode(opCode), .out_2(ALUsrc));
  RegDst regdst_1 (.Inst(opCode), .RegDest(RegDst));
  NextPC nextpc_1 (.opCode(opCode), .out_2(nPC_Sel));
  ALUop aluop_1 (.opCode(opCode), .out_2(ALUoperation));
  Rtype rtype_1 (.opCode(opCode), .out_2(Rtype));

  assign ALUOp = opCode;
endmodule

module RegDst (
  input  [3:0] Inst,
  output [1:0] RegDest
);

  Multiplexer #(.select(4), .width(2)) multiplexer_1 (
    .in0(2'b01), .in1(2'b10), .in2(2'b00), .in3(2'b00), .in4(2'b00), .in5(2'b00), .in6(2'b00), .in7(2'b00),
    .in8(2'b00), .in9(2'b00), .in10(2'b00), .in11(2'b00), .in12(2'b00), .in13(2'b00), .in14(2'b00),
    .in15(2'b00), .out(RegDest), .sel(Inst));  // open: en

  // Notes on the sheet:
  //   Should send 2 if jal, 1 if R type, else 0
  //   jal
endmodule

module RegWrite (
  input  [3:0] opCode,
  output out_2
);

  Multiplexer #(.select(4)) multiplexer_1 (
    .in0(1'b1), .in1(1'b1), .in2(1'b0), .in3(1'b0), .in4(1'b0), .in5(1'b1), .in6(1'b1), .in7(1'b1),
    .in8(1'b0), .in9(1'b0), .in10(1'b1), .in11(1'b1), .in12(1'b0), .in13(1'b0), .in14(1'b0), .in15(1'b0),
    .out(out_2), .sel(opCode));  // open: en
endmodule

module Display (
  input  [3:0] opCode,
  output out_2
);

  Multiplexer #(.select(4)) multiplexer_1 (
    .in0(1'b0), .in1(1'b0), .in2(1'b0), .in3(1'b0), .in4(1'b0), .in5(1'b0), .in6(1'b0), .in7(1'b0),
    .in8(1'b0), .in9(1'b0), .in10(1'b0), .in11(1'b0), .in12(1'b1), .in13(1'b0), .in14(1'b0), .in15(1'b0),
    .out(out_2), .sel(opCode));  // open: en
endmodule

module MemWrite (
  input  [3:0] opCode,
  output out_2
);

  Multiplexer #(.select(4)) multiplexer_1 (
    .in0(1'b0), .in1(1'b0), .in2(1'b0), .in3(1'b0), .in4(1'b0), .in5(1'b0), .in6(1'b0), .in7(1'b0),
    .in8(1'b0), .in9(1'b1), .in10(1'b0), .in11(1'b0), .in12(1'b0), .in13(1'b0), .in14(1'b0), .in15(1'b0),
    .out(out_2), .sel(opCode));  // open: en
endmodule

module Jal (
  input  [3:0] opCode,
  output out_2
);

  Multiplexer #(.select(4)) multiplexer_1 (
    .in0(1'b0), .in1(1'b1), .in2(1'b0), .in3(1'b0), .in4(1'b0), .in5(1'b0), .in6(1'b0), .in7(1'b0),
    .in8(1'b0), .in9(1'b0), .in10(1'b0), .in11(1'b0), .in12(1'b0), .in13(1'b0), .in14(1'b0), .in15(1'b0),
    .out(out_2), .sel(opCode));  // open: en
endmodule

module Jump (
  input  [3:0] opCode,
  output out_2
);

  Multiplexer #(.select(4)) multiplexer_1 (
    .in0(1'b0), .in1(1'b0), .in2(1'b1), .in3(1'b1), .in4(1'b0), .in5(1'b0), .in6(1'b0), .in7(1'b0),
    .in8(1'b0), .in9(1'b0), .in10(1'b0), .in11(1'b0), .in12(1'b0), .in13(1'b0), .in14(1'b0), .in15(1'b0),
    .out(out_2), .sel(opCode));  // open: en
endmodule

module Beq (
  input  [3:0] opCode,
  output out_2
);

  Multiplexer #(.select(4)) multiplexer_1 (
    .in0(1'b0), .in1(1'b0), .in2(1'b0), .in3(1'b0), .in4(1'b1), .in5(1'b0), .in6(1'b0), .in7(1'b0),
    .in8(1'b0), .in9(1'b0), .in10(1'b0), .in11(1'b0), .in12(1'b0), .in13(1'b0), .in14(1'b0), .in15(1'b0),
    .out(out_2), .sel(opCode));  // open: en
endmodule

module Bne (
  input  [3:0] opCode,
  output out_2
);

  Multiplexer #(.select(4)) multiplexer_1 (
    .in0(1'b0), .in1(1'b0), .in2(1'b0), .in3(1'b0), .in4(1'b0), .in5(1'b0), .in6(1'b0), .in7(1'b0),
    .in8(1'b1), .in9(1'b0), .in10(1'b0), .in11(1'b0), .in12(1'b0), .in13(1'b0), .in14(1'b0), .in15(1'b0),
    .out(out_2), .sel(opCode));  // open: en
endmodule

module MemToReg (
  input  [3:0] opCode,
  output out_2
);

  Multiplexer #(.select(4)) multiplexer_1 (
    .in0(1'b0), .in1(1'b0), .in2(1'b0), .in3(1'b0), .in4(1'b0), .in5(1'b0), .in6(1'b0), .in7(1'b0),
    .in8(1'b0), .in9(1'b0), .in10(1'b0), .in11(1'b1), .in12(1'b0), .in13(1'b0), .in14(1'b0), .in15(1'b0),
    .out(out_2), .sel(opCode));  // open: en
endmodule

module BranchOJump (
  input  [3:0] opCode,
  output out_2
);

  Multiplexer #(.select(4)) multiplexer_1 (
    .in0(1'b0), .in1(1'b1), .in2(1'b1), .in3(1'b1), .in4(1'b1), .in5(1'b0), .in6(1'b0), .in7(1'b0),
    .in8(1'b1), .in9(1'b0), .in10(1'b0), .in11(1'b0), .in12(1'b0), .in13(1'b0), .in14(1'b0), .in15(1'b0),
    .out(out_2), .sel(opCode));  // open: en
endmodule

module SignExtend (
  input  [3:0] opCode,
  output SignExtend
);

  Multiplexer #(.select(4)) multiplexer_1 (
    .in0(1'b0), .in1(1'b0), .in2(1'b0), .in3(1'b0), .in4(1'b1), .in5(1'b1), .in6(1'b0), .in7(1'b0),
    .in8(1'b1), .in9(1'b0), .in10(1'b0), .in11(1'b1), .in12(1'b0), .in13(1'b0), .in14(1'b0), .in15(1'b0),
    .out(SignExtend), .sel(opCode));  // open: en
endmodule

module ALUsrc (
  input  [3:0] opCode,
  output out_2
);

  Multiplexer #(.select(4)) multiplexer_1 (
    .in0(1'b0), .in1(1'b0), .in2(1'b0), .in3(1'b0), .in4(1'b0), .in5(1'b1), .in6(1'b1), .in7(1'b1),
    .in8(1'b0), .in9(1'b1), .in10(1'b1), .in11(1'b1), .in12(1'b1), .in13(1'b1), .in14(1'b1), .in15(1'b1),
    .out(out_2), .sel(opCode));  // open: en
endmodule

module ALUcontroller (
  input  [3:0] opcode,
  input  [5:0] \function ,
  output [3:0] opcode_2
);

  wire [3:0] bit_extender_1_out;

  Bit_Extender #(.in_width(6), .out_width(4)) bit_extender_1 (.in(\function ), .out(bit_extender_1_out));
  Multiplexer #(.select(4), .width(4)) multiplexer_1 (
    .in0(bit_extender_1_out), .in5(4'b0000), .in6(4'b0111), .in7(4'b0110), .in9(4'b0000), .in10(4'b1010),
    .in11(4'b0000), .out(opcode_2), .sel(opcode));  // open: in1, in2, in3, in4, in8, in12, in13, in14, in15, en
endmodule

// NOOP
module Noop (
  input  [15:0] Instruction,
  input  [2:0] nPC_sel,
  input  BEQGOOD,
  input  ALUequal,
  input  BNEGOOD,
  input  Jump,
  output [15:0] InstructionOut
);

  wire and_1_out, and_2_out, and_3_out, and_4_out, comparator_1_eq, comparator_2_eq, not_1_out, or_1_out;

  Comparator #(.width(3)) comparator_1 (.a(nPC_sel), .b(3'b001), .eq(comparator_1_eq));  // open: gt, lt
  not not_1 (not_1_out, ALUequal);
  and and_1 (and_1_out, BEQGOOD, ALUequal);
  and and_2 (and_2_out, not_1_out, BNEGOOD);
  Comparator #(.width(3)) comparator_2 (.a(nPC_sel), .b(3'b010), .eq(comparator_2_eq));  // open: gt, lt
  and and_3 (and_3_out, comparator_1_eq, BEQGOOD);
  and and_4 (and_4_out, BNEGOOD, comparator_2_eq);
  Multiplexer #(.width(16)) multiplexer_1 (
    .in0(Instruction), .in1(16'h6), .out(InstructionOut), .sel(or_1_out));  // open: en
  or or_1 (or_1_out, and_3_out, and_3_out, and_1_out, and_2_out, and_4_out, Jump);

  // Other names for the same wires on the sheet: Selector[2:0] = nPC_sel

  // Notes on the sheet:
  //   Determines whether we want to send noop or not (only if we branch or jump)
  //   x0006 is Noop
endmodule

// PCCounter
module PCcounter (
  input  [15:0] PC,
  input  [15:0] signExtImm,
  input  BEQpass,
  input  BNEpass,
  input  [11:0] jAddr,
  input  [15:0] rs,
  input  [2:0] npc_Sel,
  output [15:0] nxtPC
);

  wire or_2_out;
  wire [15:0] adder_2_out, and_1_out, bit_extender_1_out, multiplexer_1_out, or_1_out, PC_0001;

  Adder #(.width(16)) adder_1 (.a(PC), .b(16'h1), .out(PC_0001));  // open: cin, cout
  assign bit_extender_1_out = {{4{1'b0}}, jAddr};  // Bit_Extender bit_extender_1
  assign and_1_out = PC & 16'hf000;  // AND_Gate and_1, 16 bits wide
  Adder #(.width(16)) adder_2 (.a(PC), .b(signExtImm), .out(adder_2_out));  // open: cin, cout
  assign or_1_out = and_1_out | bit_extender_1_out;  // OR_Gate or_1, 16 bits wide
  or or_2 (or_2_out, BEQpass, BNEpass);
  Multiplexer #(.width(16)) multiplexer_1 (
    .in0(PC_0001), .in1(adder_2_out), .out(multiplexer_1_out), .sel(or_2_out));  // open: en
  Multiplexer #(.select(3), .width(16), .enable("false")) multiplexer_2 (
    .in0(PC), .in1(or_1_out), .in2(or_1_out), .in3(multiplexer_1_out), .in4(multiplexer_1_out), .in5(rs),
    .out(nxtPC), .sel(npc_Sel));  // open: in6, in7
endmodule

module displayer (
  input  Controler,
  input  clk,
  input  [15:0] rs,
  input  [15:0] Immediate
);
endmodule

module ALUop (
  input  [3:0] opCode,
  output out_2
);

  Multiplexer #(.select(4)) multiplexer_1 (
    .in0(1'b1), .in1(1'b0), .in2(1'b0), .in3(1'b0), .in4(1'b0), .in5(1'b0), .in6(1'b0), .in7(1'b0),
    .in8(1'b0), .in9(1'b0), .in10(1'b0), .in11(1'b0), .in12(1'b0), .in13(1'b0), .in14(1'b0), .in15(1'b0),
    .out(out_2), .sel(opCode));  // open: en
endmodule

module NextPC (
  input  [3:0] opCode,
  output [2:0] out_2
);

  Multiplexer #(.select(4), .width(3)) multiplexer_1 (
    .in0(3'b000), .in1(3'b010), .in2(3'b001), .in3(3'b101), .in4(3'b100), .in5(3'b000), .in6(3'b000),
    .in7(3'b000), .in8(3'b011), .in9(3'b000), .in10(3'b000), .in11(3'b000), .in12(3'b000), .in13(3'b000),
    .in14(3'b000), .in15(3'b000), .out(out_2), .sel(opCode));  // open: en
endmodule

module Rtype (
  input  [3:0] opCode,
  output out_2
);

  Multiplexer #(.select(4)) multiplexer_1 (
    .in0(1'b1), .in1(1'b0), .in2(1'b0), .in3(1'b0), .in4(1'b0), .in5(1'b0), .in6(1'b0), .in7(1'b0),
    .in8(1'b0), .in9(1'b0), .in10(1'b0), .in11(1'b0), .in12(1'b0), .in13(1'b0), .in14(1'b0), .in15(1'b0),
    .out(out_2), .sel(opCode));  // open: en
endmodule
